// Logisim project Arch_EVM222.circ as structural Verilog
module HalfAdder (
  input  a,
  input  b,
  output s,
  output carry
);

  and and_1 (carry, a, b);
  xor xor_1 (s, a, b);
endmodule

module FullAdder (
  input  Cin,
  input  a,
  input  b,
  output s,
  output Cout
);

  wire halfadder_1_carry, halfadder_1_s, halfadder_2_carry;

  HalfAdder halfadder_1 (.a(a), .b(b), .s(halfadder_1_s), .carry(halfadder_1_carry));
  HalfAdder halfadder_2 (.a(Cin), .b(halfadder_1_s), .s(s), .carry(halfadder_2_carry));
  or or_1 (Cout, halfadder_2_carry, halfadder_1_carry);
endmodule

module CPA (
  input  Cin,
  input  [3:0] a,
  input  [3:0] b,
  output [3:0] S,
  output Cout
);

  wire fulladder_1_cout, fulladder_2_cout, fulladder_3_cout;

  FullAdder fulladder_1 (.Cin(Cin), .a(a[0]), .b(b[0]), .s(S[0]), .Cout(fulladder_1_cout));
  FullAdder fulladder_2 (.Cin(fulladder_1_cout), .a(a[1]), .b(b[1]), .s(S[1]), .Cout(fulladder_2_cout));
  FullAdder fulladder_3 (.Cin(fulladder_2_cout), .a(a[2]), .b(b[2]), .s(S[2]), .Cout(fulladder_3_cout));
  FullAdder fulladder_4 (.Cin(fulladder_3_cout), .a(a[3]), .b(b[3]), .s(S[3]), .Cout(Cout));
endmodule

module Incrementer (
  input  Cin,
  input  [3:0] a,
  output [3:0] out_3
);

  CPA cpa_1 (.Cin(Cin), .a(a), .b(4'b0001), .S(out_3));  // open: Cout
endmodule

module Sub (
  input  Cin,
  input  [3:0] a,
  input  [3:0] b,
  output [3:0] S,
  output Cout
);

  wire [3:0] not_1_out;

  assign not_1_out = ~b;  // NOT_Gate not_1, 4 bits wide
  CPA cpa_1 (.Cin(Cin), .a(a), .b(not_1_out), .S(S), .Cout(Cout));
endmodule

module SubSum (
  input  [3:0] b,
  input  [3:0] a,
  input  in_3
);

  wire [3:0] not_1_out;

  assign not_1_out = ~b;  // NOT_Gate not_1, 4 bits wide
  // HalfAdder halfadder_1: pin names not known; wires that end beside it: b, not_1_out
endmodule
